// Logisim project BCD to Excess-3 Converter.circ as structural Verilog: 1 circuit, main circuit main
module main (
  input  B3,
  input  B2,
  input  B1,
  input  B0,
  output out_5,
  output out_6,
  output out_7,
  output out_8
);

  wire and_1_out, or_2_out, xor_2_out;

  or or_1 (out_5, B3, and_1_out);
  or or_2 (or_2_out, B0, B1);
  and and_1 (and_1_out, or_2_out, B2);
  xor xor_1 (out_6, or_2_out, B2);
  xor xor_2 (xor_2_out, B1, B0);
  not not_1 (out_7, xor_2_out);
  not not_2 (out_8, B0);

  // Notes on the sheet:
  //   INPUT IN BCD
  //   OUTPUT IN EXCESS 3
endmodule
